# Fritzing sketch Model (saved by Fritzing 0.9.3b)
circuit board: 8.46667cm x 5.64444cm
breadboards: 2

parts:
  Part1 = Arduino Mega 2560 (Rev3)
  SRAM_Chip = IC, DIP package, 28 pins [chip_label=CY62256N]
  microSD2 = MicroSD Breakout
  Componente4 = sensor_biometrico

nets:
  N1: Part1.A8, Part1.D9_PWM, SRAM_Chip.pin28
  GND: Part1.GND, SRAM_Chip.pin14, microSD2.GND, Componente4.GND
  N2: Part1.D13_PWM, SRAM_Chip.pin20
  N3: Part1.D12_PWM, SRAM_Chip.pin22
  N4: Part1.D11_PWM, SRAM_Chip.pin27
  5V: Part1.5V, microSD2.5V, Componente4.VCC
  N5: Part1.D0_RX0, Componente4.RX
  N6: Part1.D1_TX0, Componente4.TX
  N7: Part1.D7_PWM, microSD2.CS
  N8: Part1.D22, SRAM_Chip.pin10
  N9: Part1.D23, SRAM_Chip.pin9
  N10: Part1.D24, SRAM_Chip.pin8
  N11: Part1.D25, SRAM_Chip.pin7
  N12: Part1.D26, SRAM_Chip.pin6
  N13: Part1.D27, SRAM_Chip.pin5
  N14: Part1.D28, SRAM_Chip.pin4
  N15: Part1.D29, SRAM_Chip.pin3
  N16: Part1.D31, SRAM_Chip.pin1
  N17: Part1.D32, SRAM_Chip.pin26
  N18: Part1.D33, SRAM_Chip.pin2
  N19: Part1.D34, SRAM_Chip.pin23
  N20: Part1.D35, SRAM_Chip.pin21
  N21: Part1.D36, SRAM_Chip.pin24
  N22: Part1.D37, SRAM_Chip.pin25
  N23: Part1.D42, SRAM_Chip.pin19
  N24: Part1.D43, SRAM_Chip.pin18
  N25: Part1.D44, SRAM_Chip.pin17
  N26: Part1.D45, SRAM_Chip.pin16
  N27: Part1.D46, SRAM_Chip.pin15
  N28: Part1.D47, SRAM_Chip.pin13
  N29: Part1.D48, SRAM_Chip.pin12
  N30: Part1.D49, SRAM_Chip.pin11
  N31: Part1.D50, microSD2.DI
  N32: Part1.D51, microSD2.DO
  N33: Part1.D52, microSD2.CLK

custom parts:
  MicroSD Breakout: 5V-ready microSD Breakout with Level Shifter
  sensor_biometrico: Adafruit Optical Fingerprint Sensor

// code stored in the sketch: Untitled2.ino
#include <Adafruit_Fingerprint.h>



#if (defined(__AVR__) || defined(ESP8266)) && !defined(__AVR_ATmega2560__)
// For UNO and others without hardware serial, we must use software serial...
// pin #2 is IN from sensor (GREEN wire)
// pin #3 is OUT from arduino  (WHITE wire)
// Set up the serial port to use softwareserial..
SoftwareSerial mySerial(2, 3);


#else
// On Leonardo/M0/etc, others with hardware serial, use hardware serial!
// #0 is green wire, #1 is white
#define mySerial Serial1


#endif



Adafruit_Fingerprint finger = Adafruit_Fingerprint(&mySerial);


uint8_t id;


void setup()
{
  Serial.begin(9600);
  while (!Serial);  // For Yun/Leo/Micro/Zero/...
  delay(100);
  Serial.println("\n\nAdafruit Fingerprint sensor enrollment");


  // set the data rate for the sensor serial port
  finger.begin(57600);


  if (finger.verifyPassword()) {
    Serial.println("Found fingerprint sensor!");
  } else {
    Serial.println("Did not find fingerprint sensor :(");
    while (1) { delay(1); }
  }


  Serial.println(F("Reading sensor parameters"));
  finger.getParameters();
  Serial.print(F("Status: 0x")); Serial.println(finger.status_reg, HEX);
  Serial.print(F("Sys ID: 0x")); Serial.println(finger.system_id, HEX);
  Serial.print(F("Capacity: ")); Serial.println(finger.capacity);
  Serial.print(F("Security level: ")); Serial.println(finger.security_level);
  Serial.print(F("Device address: ")); Serial.println(finger.device_addr, HEX);
  Serial.print(F("Packet len: ")); Serial.println(finger.packet_len);
  Serial.print(F("Baud rate: ")); Serial.println(finger.baud_rate);
}


uint8_t readnumber(void) {
  uint8_t num = 0;


  while (num == 0) {
    while (! Serial.available());
    num = Serial.parseInt();
  }
  return num;
}


void loop()                     // run over and over again
{
  Serial.println("Ready to enroll a fingerprint!");
  Serial.println("Please type in the ID # (from 1 to 127) you want to save this finger as...");
  id = readnumber();
  if (id == 0) {// ID #0 not allowed, try again!
     return;
  }
  Serial.print("Enrolling ID #");
  Serial.println(id);


  while (!  getFingerprintEnroll() );
}


uint8_t getFingerprintEnroll() {


  int p = -1;
  Serial.print("Waiting for valid finger to enroll as #"); Serial.println(id);
  while (p != FINGERPRINT_OK) {
    p = finger.getImage();
    switch (p) {
    case FINGERPRINT_OK:
      Serial.println("Image taken");
      break;
    case FINGERPRINT_NOFINGER:
      Serial.println(".");
      break;
    case FINGERPRINT_PACKETRECIEVEERR:
      Serial.println("Communication error");
      break;
    case FINGERPRINT_IMAGEFAIL:
      Serial.println("Imaging error");
      break;
    default:
      Serial.println("Unknown error");
      break;
    }
  }


  // OK success!


  p = finger.image2Tz(1);
  switch (p) {
    case FINGERPRINT_OK:
      Serial.println("Image converted");
      break;
    case FINGERPRINT_IMAGEMESS:
      Serial.println("Image too messy");
      return p;
    case FINGERPRINT_PACKETRECIEVEERR:
      Serial.println("Communication error");
      return p;
    case FINGERPRINT_FEATUREFAIL:
      Serial.println("Could not find fingerprint features");
      return p;
    case FINGERPRINT_INVALIDIMAGE:
      Serial.println("Could not find fingerprint features");
      return p;
    default:
      Serial.println("Unknown error");
      return p;
  }


  Serial.println("Remove finger");
  delay(2000);
  p = 0;
  while (p != FINGERPRINT_NOFINGER) {
    p = finger.getImage();
  }
  Serial.print("ID "); Serial.println(id);
  p = -1;
  Serial.println("Place same finger again");
  while (p != FINGERPRINT_OK) {
    p = finger.getImage();
    switch (p) {
    case FINGERPRINT_OK:
      Serial.println("Image taken");
      break;
    case FINGERPRINT_NOFINGER:
      Serial.print(".");
      break;
    case FINGERPRINT_PACKETRECIEVEERR:
      Serial.println("Communication error");
      break;
    case FINGERPRINT_IMAGEFAIL:
      Serial.println("Imaging error");
      break;
    default:
      Serial.println("Unknown error");
      break;
    }
  }


  // OK success!


  p = finger.image2Tz(2);
  switch (p) {
    case FINGERPRINT_OK:
      Serial.println("Image converted");
      break;
    case FINGERPRINT_IMAGEMESS:
      Serial.println("Image too messy");
      return p;
    case FINGERPRINT_PACKETRECIEVEERR:
      Serial.println("Communication error");
      return p;
    case FINGERPRINT_FEATUREFAIL:
      Serial.println("Could not find fingerprint features");
      return p;
    case FINGERPRINT_INVALIDIMAGE:
      Serial.println("Could not find fingerprint features");
      return p;
    default:
      Serial.println("Unknown error");
      return p;
  }


  // OK converted!
  Serial.print("Creating model for #");  Serial.println(id);


  p = finger.createModel();
  if (p == FINGERPRINT_OK) {
    Serial.println("Prints matched!");
  } else if (p == FINGERPRINT_PACKETRECIEVEERR) {
    Serial.println("Communication error");
    return p;
  } else if (p == FINGERPRINT_ENROLLMISMATCH) {
    Serial.println("Fingerprints did not match");
    return p;
  } else {
    Serial.println("Unknown error");
    return p;
  }


  Serial.print("ID "); Serial.println(id);
  p = finger.storeModel(id);
  if (p == FINGERPRINT_OK) {
    Serial.println("Stored!");
  } else if (p == FINGERPRINT_PACKETRECIEVEERR) {
    Serial.println("Communication error");
    return p;
  } else if (p == FINGERPRINT_BADLOCATION) {
    Serial.println("Could not store in that location");
    return p;
  } else if (p == FINGERPRINT_FLASHERR) {
    Serial.println("Error writing to flash");
    return p;
  } else {
    Serial.println("Unknown error");
    return p;
  }


  return true;
}
